// Digital circuit 3bit ROR.dig as structural Verilog
module _3bit_ROR (
  input  [2:0] A_2_0,
  input  [2:0] B_2_0,
  output [2:0] O_2_0
);

  Multiplexer #(.Selector_Bits(3)) multiplexer_1 (
    .sel(B_2_0), .in_0(A_2_0[2]), .in_1(A_2_0[0]), .in_2(A_2_0[1]), .in_3(A_2_0[2]), .in_4(1'b0),
    .in_5(1'b0), .in_6(1'b0), .in_7(1'b0), .out(O_2_0[2]));
  Multiplexer #(.Selector_Bits(3)) multiplexer_2 (
    .sel(B_2_0), .in_0(A_2_0[1]), .in_1(A_2_0[2]), .in_2(A_2_0[0]), .in_3(A_2_0[1]), .in_4(1'b0),
    .in_5(1'b0), .in_6(1'b0), .in_7(1'b0), .out(O_2_0[1]));
  Multiplexer #(.Selector_Bits(3)) multiplexer_3 (
    .sel(B_2_0), .in_0(A_2_0[0]), .in_1(A_2_0[1]), .in_2(A_2_0[2]), .in_3(A_2_0[0]), .in_4(1'b0),
    .in_5(1'b0), .in_6(1'b0), .in_7(1'b0), .out(O_2_0[0]));

  // Other names for the same wires on the sheet: A0 = A_2_0[0]; A1 = A_2_0[1]; A2 = A_2_0[2]; Sel[2:0] = B_2_0
endmodule
