// Digital circuit 3bit XOR.dig as structural Verilog
module _3bit_XOR (
  input  [2:0] A_2_0,
  input  [2:0] B_2_0,
  output [2:0] O_2_0
);

  assign O_2_0 = A_2_0 ^ B_2_0;  // XOr xor_1, 3 bits wide
endmodule
