// Digital circuit 4X17 RAM.dig as structural Verilog
module _4X17_RAM (
  input  [3:0] WA_3_0,
  input  WE,
  input  CLK,
  input  [3:0] RA1_3_0,
  input  [3:0] RA2_3_0,
  input  [16:0] WRD_16_0,
  output [16:0] RD1_16_0,
  output [16:0] RD2_16_0
);

  wire RA1_0, RA1_1, RA1_2, RA1_3, RA2_0, RA2_1, RA2_2, RA2_3, W0, W1, W2, W3, WS0, WS1, WS2, WS3;
  wire [16:0] RD1_0, RD1_1, RD1_2, RD1_3, RD2_0, RD2_1, RD2_2, RD2_3;

  Decoder #(.Selector_Bits(4)) decoder_1 (
    .sel(WA_3_0), .out_0(W0), .out_1(W1), .out_2(W2), .out_3(W3));  // open: out_4, out_5, out_6, out_7, out_8, out_9, out_10, out_11, out_12, out_13, out_14, out_15
  and and_1 (WS3, W3, WE);
  and and_2 (WS1, W1, WE);
  Decoder #(.Selector_Bits(4)) decoder_2 (
    .sel(RA1_3_0), .out_0(RA1_0), .out_1(RA1_1), .out_2(RA1_2), .out_3(RA1_3));  // open: out_4, out_5, out_6, out_7, out_8, out_9, out_10, out_11, out_12, out_13, out_14, out_15
  and and_3 (WS2, W2, WE);
  and and_4 (WS0, W0, WE);
  Decoder #(.Selector_Bits(4)) decoder_3 (
    .sel(RA2_3_0), .out_0(RA2_0), .out_1(RA2_1), .out_2(RA2_2), .out_3(RA2_3));  // open: out_4, out_5, out_6, out_7, out_8, out_9, out_10, out_11, out_12, out_13, out_14, out_15
  // _1X17_RAM _1x17_ram_1: pin names not known; wires that end beside it: RA1_3, RA2_3, WS3, WRD_16_0, CLK, RD1_3, RD2_3
  // _1X17_RAM _1x17_ram_2: pin names not known; wires that end beside it: RA1_2, RA2_2, WS2, WRD_16_0, CLK, RD1_2, RD2_2
  // _1X17_RAM _1x17_ram_3: pin names not known; wires that end beside it: RA1_1, RA2_1, WS1, WRD_16_0, CLK, RD1_1, RD2_1
  // _1X17_RAM _1x17_ram_4: pin names not known; wires that end beside it: RA1_0, RA2_0, WS0, WRD_16_0, CLK, RD1_0, RD2_0
  assign RD1_16_0 = RD1_3 | RD1_2 | RD1_1 | RD1_0;  // Or or_1, 17 bits wide
  assign RD2_16_0 = RD2_3 | RD2_2 | RD2_1 | RD2_0;  // Or or_2, 17 bits wide

  // Other names for the same wires on the sheet: WRD[16:0] = WRD_16_0
endmodule
