// Digital circuit 4bit_Reister_Set.dig as structural Verilog
module _4bit_Reister_Set (
  input  [1:0] WR_1_0,
  input  CLK,
  input  [2:0] WRD_3_0,
  input  [1:0] RA_1_0,
  input  [1:0] RB_1_0,
  input  WE,
  output [2:0] A_2_0,
  output [2:0] B_2_0
);

  wire A0, A1, A2, A3, D0, D1, D2, D3;
  wire [2:0] R0, R1, R2, R3;

  and and_1 (D3, WE, A3);
  and and_2 (D1, WE, A1);
  and and_3 (D2, WE, A2);
  and and_4 (D0, WE, A0);
  Decoder #(.Selector_Bits(2)) decoder_1 (.sel(WR_1_0), .out_0(A0), .out_1(A1), .out_2(A2), .out_3(A3));
  // _3bit_Reg _3bit_reg_1: pin names not known; wires that end beside it: WRD_3_0, D3, CLK, R3
  // _3bit_Reg _3bit_reg_2: pin names not known; wires that end beside it: WRD_3_0, D2, CLK, R2
  // _3bit_Reg _3bit_reg_3: pin names not known; wires that end beside it: WRD_3_0, D1, CLK, R1
  // _3bit_Reg _3bit_reg_4: pin names not known; wires that end beside it: WRD_3_0, D0, CLK, R0
  Multiplexer #(.Selector_Bits(2), .Bits(3)) multiplexer_1 (
    .sel(RA_1_0), .in_0(R0), .in_1(R1), .in_2(R2), .in_3(R3), .out(A_2_0));
  Multiplexer #(.Selector_Bits(2), .Bits(3)) multiplexer_2 (
    .sel(RB_1_0), .in_0(R0), .in_1(R1), .in_2(R2), .in_3(R3), .out(B_2_0));
endmodule
