// Digital circuit CPU_Final_Design.dig as structural Verilog
module CPU_Final_Design (
  input  [3:0] WA_3_0,
  input  [16:0] WRD_16_0,
  input  WE,
  input  CLK,
  input  PC_EN,
  input  [3:0] RA2_3_0,
  output [16:0] RD2_16_0,
  output [2:0] R_2_0,
  output [1:0] RA_1_0,
  output [2:0] R2_2_0,
  output [1:0] RB_1_0,
  output [2:0] A_2_0,
  output [2:0] B_2_0,
  output [1:0] WR_1_0,
  output [3:0] JMP_Address
);

  wire _1bit_reg_1_p4, CF, CPU_CLK, Imm_sel, JMP_Sel, Reg_EN;
  wire [1:0] Op;
  wire [2:0] _4bit_reister_set_1_b_2_0;
  wire [3:0] _4bit_pc_adder_1_p1, _4bit_pc_adder_1_p2, multiplexer_1_out;
  wire [7:0] xx;
  wire [16:13] _4x17_ram_1_rd1_16_0;

  Multiplexer #(.Bits(4)) multiplexer_1 (
    .sel(JMP_Sel), .in_0(_4bit_pc_adder_1_p1), .in_1(JMP_Address), .out(multiplexer_1_out));
  // _4bit_PC_Adder _4bit_pc_adder_1: pin names not known; wires that end beside it: _4bit_pc_adder_1_p1, _4bit_pc_adder_1_p2
  // _4bit_Program_Counter _4bit_program_counter_1: pin names not known; wires that end beside it: multiplexer_1_out, CPU_CLK, _4bit_pc_adder_1_p2
  and and_1 (CPU_CLK, CLK, PC_EN);
  _4X17_RAM _4x17_ram_1 (
    .WA_3_0(_4bit_pc_adder_1_p2), .RA1_3_0(RA2_3_0), .RA2_3_0(WA_3_0), .WRD_16_0(WRD_16_0), .WE(WE),
    .CLK(CLK), .RD1_16_0({_4x17_ram_1_rd1_16_0, JMP_Address, R2_2_0[0], xx}), .RD2_16_0(RD2_16_0));
  // _1bit_Reg _1bit_reg_1: pin names not known; wires that end beside it: CF, CPU_CLK, 1'b1, _1bit_reg_1_p4
  // Control_Unit control_unit_1: pin names not known; wires that end beside it: _4x17_ram_1_rd1_16_0, CF, Op, Reg_EN, Imm_sel, JMP_Sel
  _4bit_Reister_Set _4bit_reister_set_1 (
    .WR_1_0(JMP_Address[3:2]), .CLK(CPU_CLK), .WE(Reg_EN), .WRD_3_0(R_2_0), .RA_1_0(JMP_Address[3:2]),
    .RB_1_0(JMP_Address[1:0]), .A_2_0(A_2_0), .B_2_0(_4bit_reister_set_1_b_2_0));
  _3bit_ALU _3bit_alu_1 (.A_2_0(A_2_0), .B_2_0(B_2_0), .OP_1_0(Op), .O_2_0(R_2_0), .CF(_1bit_reg_1_p4));
  Multiplexer #(.Bits(3)) multiplexer_2 (
    .sel(Imm_sel), .in_0(_4bit_reister_set_1_b_2_0), .in_1({JMP_Address[1:0], R2_2_0[0]}), .out(B_2_0));

  assign R2_2_0[2:1] = JMP_Address[1:0];
  assign RA_1_0 = JMP_Address[3:2];
  assign RB_1_0 = JMP_Address[1:0];
  assign WR_1_0 = JMP_Address[3:2];

  // Other names for the same wires on the sheet: R2[2:0] = {JMP_Address[1:0], R2_2_0[0]}; JMP_Add[3:0] = JMP_Address;
  //   RB[1:0] = JMP_Address[1:0]; R1[1:0] = JMP_Address[3:2]; A[2:0] = A_2_0; B[2:0] = B_2_0; RD2[16:0] = RD2_16_0

  // Notes on the sheet:
  //   Assembly :
  //   JMP START->10000001000000000
  //   START: ADD R1,5->01000010100000000
  //   JMPTO:ADD R1,4->01000010000000000
  //   JC JMPTO->10010010000000000
  //   ADD R2,1->01000100100000000
  //   SHR R1,R2->00100001000000000
  //   NOT R1->00010000000000000
  //   Register Mode(type of Op=00)= 2bit(Type of Op)+ 2bit(Op)+2bit(Reg1)+2bit(Reg2)+9bit(don't care)
  //   Immediate Mode(type of Op=01)= 2bit(Type of Op)+ 2bit(Op)+2bit(Reg1)+3bit(Imm value)+8bit(don't care)
  //   Braching(type of Op=10)= 2bit(Type of Op)+ 2bit(Op)+4bit(JMP Add)+9bit(don't care)
  //   ADD(Op=00), NOT(Op=01), SHR(Op=10)
  //   JMP(Op=00),JC(01)
  //   ADD R1,5 = 000001101xxxxxxxx
endmodule
